# Fritzing sketch 12V DC Motor (A,B,C) Sketch  (saved by Fritzing 0.9.3b)

parts:
  Raspberry_Pi_1 = Raspberry Pi 3 [part_number=RPI-3-V1.2]
  L298N1 = L298N motor driver
  L298N2 = L298N motor driver

nets:
  N1: Raspberry_Pi_1.GPIO17, L298N1.connector15
  N2: Raspberry_Pi_1.GPIO27, L298N1.connector12
  N3: Raspberry_Pi_1.GPIO22, L298N1.connector16
  N4: Raspberry_Pi_1.GPIO10, L298N1.connector11
  N5: Raspberry_Pi_1.GPIO9, L298N1.connector13
  N6: Raspberry_Pi_1.GPIO11, L298N1.connector14
  N7: Raspberry_Pi_1.GPIO18, L298N2.connector14
  N8: Raspberry_Pi_1.GPIO15, L298N2.connector13
  N9: Raspberry_Pi_1.GPIO14, L298N2.connector11
